// Logisim project 4BitALU.circ as structural Verilog: 5 circuits, main circuit main
module Arithmetic_Unit (
  input  [3:0] A,
  input  [3:0] in_2,
  input  SUBT,
  output [3:0] out_4
);

  wire [3:0] multiplexer_1_out, not_1_out;

  assign not_1_out = ~in_2;  // NOT_Gate not_1, 4 bits wide
  Multiplexer #(.width(4)) multiplexer_1 (.in0(in_2), .in1(not_1_out), .out(multiplexer_1_out), .sel(SUBT));
  Adder #(.width(4)) adder_1 (.a(A), .b(multiplexer_1_out), .out(out_4), .cin(SUBT));  // open: cout

  // Notes on the sheet:
  //   B
endmodule

module Logic_Unit (
  input  [3:0] in_1,
  input  [3:0] in_2,
  output [3:0] out_3,
  output [3:0] out_4,
  output [3:0] out_5,
  output [3:0] out_6
);

  assign out_4 = in_1 & in_2;  // AND_Gate and_1, 4 bits wide
  assign out_5 = in_1 | in_2;  // OR_Gate or_1, 4 bits wide
  assign out_6 = in_1 ^ in_2;  // XOR_Gate xor_1, 4 bits wide

  assign out_3 = {in_1[2:0], 1'b0};

  // Notes on the sheet:
  //   A
  //   B
  //   A_SHIFT_LEFT
  //   A_AND_B
  //   A_OR_B
  //   A_XOR_B
endmodule

module ROUTING_UNIT (
  input  [3:0] in_1,
  input  [3:0] in_2,
  input  [3:0] in_3,
  input  [3:0] in_4,
  input  [3:0] in_5,
  input  [3:0] in_6,
  input  [3:0] in_7,
  input  [3:0] in_8,
  input  [2:0] in_9,
  output [3:0] out_10
);

  Multiplexer #(.select(3), .width(4)) multiplexer_1 (
    .in0(in_1), .in1(in_2), .in2(in_3), .in3(in_4), .in4(in_5), .in5(in_6), .in6(in_7), .in7(in_8),
    .out(out_10), .sel(in_9));
endmodule

module HEX_DECODER (
  input  [3:0] in_1,
  output out_2,
  output out_3,
  output out_4,
  output out_5,
  output out_6,
  output out_7,
  output out_8
);

  wire and_1_out, and_2_out, and_3_out, and_4_out, and_5_out, and_6_out, and_7_out, and_8_out, and_9_out,
       and_10_out, and_11_out, and_12_out, and_13_out, and_14_out, and_15_out, and_16_out, and_17_out,
       and_18_out, and_19_out, and_20_out, and_21_out, and_22_out, and_23_out, and_24_out, and_25_out,
       and_26_out, and_27_out, and_28_out, and_29_out, and_30_out, and_31_out, and_32_out, and_33_out,
       not_1_out, not_2_out, not_3_out, not_4_out;

  not not_1 (not_1_out, in_1[3]);
  not not_2 (not_2_out, in_1[2]);
  not not_3 (not_3_out, in_1[1]);
  not not_4 (not_4_out, in_1[0]);
  and and_1 (and_1_out, not_4_out, in_1[3]);
  and and_2 (and_2_out, not_4_out, not_2_out);
  and and_3 (and_3_out, in_1[0], in_1[2], not_1_out);
  and and_4 (and_4_out, not_3_out, not_2_out, in_1[3]);
  and and_5 (and_5_out, in_1[0], in_1[3]);
  and and_6 (and_6_out, in_1[3], not_2_out);
  and and_7 (and_7_out, not_1_out, not_4_out, in_1[1]);
  and and_8 (and_8_out, not_1_out, not_2_out, in_1[1]);
  and and_9 (and_9_out, not_1_out, in_1[2], not_3_out);
  or or_1 (out_2, and_1_out, and_2_out, and_3_out, and_4_out, in_1[1]);
  and and_10 (and_10_out, not_1_out, not_3_out, not_4_out);
  and and_11 (and_11_out, not_2_out, not_3_out);
  and and_12 (and_12_out, not_1_out, not_2_out);
  and and_13 (and_13_out, not_1_out, in_1[1], in_1[0]);
  and and_14 (and_14_out, in_1[3], not_3_out, in_1[0]);
  and and_15 (and_15_out, not_1_out, in_1[2], not_3_out);
  and and_16 (and_16_out, not_3_out, not_4_out);
  and and_17 (and_17_out, in_1[3], not_2_out);
  and and_18 (and_18_out, in_1[3], in_1[1]);
  and and_19 (and_19_out, in_1[2], not_4_out);
  or or_2 (out_8, and_5_out, and_6_out, and_7_out, and_8_out, and_9_out);
  and and_20 (and_20_out, not_1_out, not_3_out);
  and and_21 (and_21_out, not_1_out, in_1[0]);
  and and_22 (and_22_out, not_3_out, in_1[0]);
  and and_23 (and_23_out, in_1[3], not_2_out);
  and and_24 (and_24_out, not_1_out, in_1[2]);
  and and_25 (and_25_out, not_2_out, not_4_out);
  and and_26 (and_26_out, in_1[1], not_4_out);
  and and_27 (and_27_out, in_1[3], in_1[2]);
  and and_28 (and_28_out, in_1[3], in_1[1]);
  or or_3 (out_7, and_15_out, and_16_out, and_17_out, and_18_out, and_19_out);
  or or_4 (out_3, and_10_out, and_13_out, and_14_out, and_11_out, and_12_out);
  or or_5 (out_4, and_20_out, and_21_out, and_22_out, and_23_out, and_24_out);
  and and_29 (and_29_out, not_2_out, not_4_out);
  and and_30 (and_30_out, not_4_out, in_1[1]);
  and and_31 (and_31_out, not_4_out, in_1[2], in_1[3]);
  and and_32 (and_32_out, not_2_out, in_1[1], not_1_out);
  and and_33 (and_33_out, not_1_out, in_1[2], not_3_out, in_1[0]);
  or E (out_6, and_25_out, and_26_out, and_27_out, and_28_out);
  or or_6 (out_5, and_29_out, and_30_out, and_31_out, and_32_out, and_33_out);

  // Notes on the sheet:
  //   D3
  //   D0
  //   D2
  //   D1
  //   ALU_RESULT
  //   A
  //   G
  //   B
  //   C
  //   F
  //   D
endmodule

module main (
  input  [3:0] in_1,
  input  [3:0] in_2,
  input  [2:0] in_3
);

  wire hex_decoder_1_out_2, hex_decoder_1_out_3, hex_decoder_1_out_4, hex_decoder_1_out_5,
       hex_decoder_1_out_6, hex_decoder_1_out_7, hex_decoder_1_out_8;
  wire [3:0] arithmetic_unit_1_out_4, logic_unit_1_out_3, logic_unit_1_out_4, logic_unit_1_out_5,
       logic_unit_1_out_6, routing_unit_1_out_10;

  Arithmetic_Unit arithmetic_unit_1 (.A(in_1), .in_2(in_2), .SUBT(in_3[0]), .out_4(arithmetic_unit_1_out_4));
  Logic_Unit logic_unit_1 (
    .in_1(in_1), .in_2(in_2), .out_3(logic_unit_1_out_3), .out_4(logic_unit_1_out_4),
    .out_5(logic_unit_1_out_5), .out_6(logic_unit_1_out_6));
  ROUTING_UNIT routing_unit_1 (
    .in_1(arithmetic_unit_1_out_4), .in_2(arithmetic_unit_1_out_4), .in_3(logic_unit_1_out_4),
    .in_4(logic_unit_1_out_5), .in_5(logic_unit_1_out_6), .in_6(logic_unit_1_out_3), .in_7(in_1),
    .in_8(in_2), .in_9(in_3), .out_10(routing_unit_1_out_10));
  HEX_DECODER hex_decoder_1 (
    .in_1(routing_unit_1_out_10), .out_2(hex_decoder_1_out_2), .out_3(hex_decoder_1_out_3),
    .out_4(hex_decoder_1_out_4), .out_5(hex_decoder_1_out_5), .out_6(hex_decoder_1_out_6),
    .out_7(hex_decoder_1_out_7), .out_8(hex_decoder_1_out_8));
  _7_Segment_Display u_7_segment_display_1 (
    .g(hex_decoder_1_out_8), .f(hex_decoder_1_out_7), .a(hex_decoder_1_out_2), .b(hex_decoder_1_out_3),
    .e(hex_decoder_1_out_6), .d(hex_decoder_1_out_5), .c(hex_decoder_1_out_4));  // open: dp

  // Notes on the sheet:
  //   OPERATION SELECT
  //   A
  //   B
endmodule
